# Fritzing sketch timer_schema (saved by Fritzing 0.9.3b)
breadboards: 1

parts:
  Componente1 = Arduino Uno (Rev3)
  Grove1 = Grove 4 Digit Display
  S1 = Pushbutton [package="[THT]"]
  LED1 = LED - 5mm [color="Red (633nm)" package="5 mm [THT]"]
  R1 = Resistor [tolerance=±5% resistance=220 package=THT]
  R2 = Resistor [tolerance=±5% resistance=220 package=THT]

nets:
  N1: Componente1.A4/SDA, Grove1.DIO
  N2: Componente1.A5/SCL, Grove1.CLK
  N3: Componente1.D9_PWM, R1.Pin_1
  N4: Componente1.D2, S1.Pin_3, S1.Pin_4, R2.Pin_1
  3V3: Componente1.3V3, Grove1.VCC, S1.Pin_1, S1.Pin_2
  GND: Componente1.GND, Grove1.GND, LED1.cathode, R2.Pin_0
  N5: LED1.anode, R1.Pin_0
